# Fritzing sketch supersecuritysystem_circut (saved by Fritzing 0.9.3b)
breadboards: 1

parts:
  Keypad4x1 = Keypad Membran 4x4
  LCM1602_IIC1 = LCM1602 IIC [part_number="LCM1602 IIC" chip_label="LCM1602 IIC" package="DIP (Dual Inline) [THT]"]
  LCD1 = LCD screen
  Part3 = RFID-RC522 [part_number=101218]
  Relay_5V1 = Keyes Relay [package=THT]
  LED1 = LED - 5mm [color="Red (633nm)" package="5 mm [THT]"]
  S1 = Pushbutton [package=THT]
  VCC1 = Battery
  J1 = Piezo Speaker
  J2 = Basic Servo
  Bauteil1 = Arduino Uno (Rev3)
  LED2 = LED - 5mm [color="Red (635nm)" package="5 mm [THT]"]
  LED3 = LED - 5mm [color="Green (565nm)" package="5 mm [THT]"]

nets:
  N1: Keypad4x1.Pin1, Bauteil1.D9_PWM
  N2: Keypad4x1.Pin2, Bauteil1.D8
  N3: Keypad4x1.Pin3, Bauteil1.D7
  N4: Keypad4x1.Pin4, Bauteil1.D6_PWM
  N5: Keypad4x1.Pin5, Bauteil1.D5_PWM
  N6: Keypad4x1.Pin6, Bauteil1.D4
  N7: Keypad4x1.Pin7, Bauteil1.D3_PWM
  N8: Keypad4x1.Pin8, Bauteil1.D2
  GND: LCM1602_IIC1.VSS, LCM1602_IIC1.GND, LCD1.VSS, Part3.GND, Relay_5V1.ground, J1.pin1, J2.gnd, Bauteil1.GND, LED2.cathode, LED3.anode
  VDD: LCM1602_IIC1.VDD, LCD1.VDD
  N9: LCM1602_IIC1.V0, LCD1.V0
  N10: LCM1602_IIC1.RS, LCD1.RS
  N11: LCM1602_IIC1.RW, LCD1.R/W
  N12: LCM1602_IIC1.E, LCD1.E
  N13: LCM1602_IIC1.D0, LCD1.DB0
  N14: LCM1602_IIC1.D1, LCD1.DB1
  N15: LCM1602_IIC1.D2, LCD1.DB2
  N16: LCM1602_IIC1.D3, LCD1.DB3
  N17: LCM1602_IIC1.D4, LCD1.DB4
  N18: LCM1602_IIC1.D5, LCD1.DB5
  N19: LCM1602_IIC1.D6, LCD1.DB6
  N20: LCM1602_IIC1.D7, LCD1.DB7
  N21: LCM1602_IIC1.A, LCD1.LED+
  N22: LCM1602_IIC1.K, LCD1.LED-
  VCC: LCM1602_IIC1.VCC, Part3.3.3V, Relay_5V1.power, S1.leg0, J2.vcc, Bauteil1.5V
  N23: LCM1602_IIC1.SDA, Bauteil1.A4/SDA
  N24: LCM1602_IIC1.SCL, Bauteil1.A5/SCL
  N25: Part3.SDA, Bauteil1.D10_PWM/SS
  N26: Part3.SCK, Bauteil1.D13/SCK
  N27: Part3.MOSI, Bauteil1.D11_PWM/MOSI
  N28: Part3.MISO, Bauteil1.D12/MISO
  N29: Relay_5V1.signal, Bauteil1.A3
  N30: Relay_5V1.NC, LED1.cathode
  N31: Relay_5V1.C, VCC1.+
  N32: S1.leg1, Bauteil1.A2
  N33: J1.pin2, Bauteil1.A1
  N34: J2.pulse, Bauteil1.A0
  N35: Bauteil1.D0/RX, LED2.anode
  N36: Bauteil1.D1/TX, LED3.cathode

notes:
  TASER
  Insert Chipcard
  Status LEDs
  Klingel
  Tür (Schloss)
  Chipcard Reader

custom parts:
  Keypad Membran 4x4: Membrane Keypad 4x4 Matrix
  LCM1602 IIC: I2C-Module to use a 1602 or 2004 LCD on with the wire.h libory Serial LCD Modul
  Keyes Relay: The Keyes 5V relay module is suitable for SCM development, home appliance control. It uses a 5V~12V TIL control signal which can control DC / AC signal.
